// Logisim project 1011 Detector.circ as structural Verilog: 2 circuits, main circuit main
module main (
  input  in_1
);

  wire clock_1_out, nand_1_out, not_1_out, not_2_out, not_3_out;
  wire [3:0] j_k_ff_1_q, j_k_ff_5_q;

  nand nand_1 (nand_1_out, not_2_out, j_k_ff_1_q[1], not_3_out, j_k_ff_1_q[3]);
  Clock clock_1 (.out(clock_1_out));
  not not_1 (not_1_out, nand_1_out);
  J_K_Flip_Flop j_k_ff_1 (
    .J(in_1), .clk(clock_1_out), .K(in_1), .Q(j_k_ff_1_q[0]), .reset(not_1_out));  // open: Qn, preset, en
  J_K_Flip_Flop j_k_ff_2 (
    .J(in_1), .clk(j_k_ff_1_q[0]), .K(in_1), .Q(j_k_ff_1_q[1]), .reset(not_1_out));  // open: Qn, preset, en
  J_K_Flip_Flop j_k_ff_3 (
    .J(in_1), .clk(j_k_ff_1_q[1]), .K(in_1), .Q(j_k_ff_1_q[2]), .reset(not_1_out));  // open: Qn, preset, en
  J_K_Flip_Flop j_k_ff_4 (
    .J(in_1), .clk(j_k_ff_1_q[2]), .K(in_1), .Q(j_k_ff_1_q[3]), .reset(not_1_out));  // open: Qn, preset, en
  J_K_Flip_Flop j_k_ff_5 (
    .J(in_1), .clk(j_k_ff_1_q[3]), .K(in_1), .Q(j_k_ff_5_q[0]), .reset(not_1_out));  // open: Qn, preset, en
  J_K_Flip_Flop j_k_ff_6 (
    .J(in_1), .clk(j_k_ff_5_q[0]), .K(in_1), .Q(j_k_ff_5_q[1]), .reset(not_1_out));  // open: Qn, preset, en
  J_K_Flip_Flop j_k_ff_7 (
    .J(in_1), .clk(j_k_ff_5_q[1]), .K(in_1), .Q(j_k_ff_5_q[2]), .reset(not_1_out));  // open: Qn, preset, en
  J_K_Flip_Flop j_k_ff_8 (
    .J(in_1), .clk(j_k_ff_5_q[2]), .K(in_1), .Q(j_k_ff_5_q[3]), .reset(not_1_out));  // open: Qn, preset, en
  not not_2 (not_2_out, j_k_ff_1_q[0]);
  not not_3 (not_3_out, j_k_ff_1_q[2]);
  Hex_Digit_Display hex_digit_display_1 (.value(j_k_ff_5_q));  // open: dp
  Hex_Digit_Display hex_digit_display_2 (.value(j_k_ff_1_q));  // open: dp
endmodule

module _1011 (
  input  X,
  output Z
);

  wire clock_1_out, d_ff_1_q, d_ff_2_q, d_ff_3_q, nand_1_out, nand_2_out, nand_3_out, nand_4_out, nand_5_out,
       nand_6_out, nand_7_out, nand_8_out, nand_9_out, nand_10_out, nand_11_out, nand_12_out, nand_13_out,
       nand_14_out, nand_15_out, nand_16_out, nand_17_out, nand_18_out, nand_19_out, nand_20_out,
       nand_21_out, nand_22_out, nand_23_out, nand_24_out, nand_25_out, nand_26_out, nand_27_out,
       nand_28_out, nand_29_out, nand_30_out, nand_31_out, nand_32_out, nand_33_out, nand_34_out,
       nand_35_out, nand_36_out, nand_37_out, nand_38_out, nand_39_out, nand_40_out, nand_41_out,
       nand_42_out, nand_43_out, nand_44_out, nand_45_out, nand_46_out, nand_47_out, nand_49_out,
       nand_50_out, nand_51_out, nand_52_out, nand_53_out, nand_54_out;

  nand nand_1 (nand_1_out, d_ff_1_q, d_ff_1_q);
  nand nand_2 (nand_2_out, d_ff_1_q, d_ff_1_q);
  nand nand_3 (nand_3_out, d_ff_1_q, d_ff_1_q);
  nand nand_4 (nand_4_out, d_ff_3_q, d_ff_3_q);
  nand nand_5 (nand_5_out, d_ff_1_q, d_ff_1_q);
  nand nand_6 (nand_6_out, d_ff_2_q, d_ff_2_q);
  nand nand_7 (nand_7_out, d_ff_1_q, d_ff_1_q);
  nand nand_8 (nand_8_out, d_ff_3_q, d_ff_3_q);
  nand nand_9 (nand_9_out, d_ff_2_q, d_ff_2_q);
  nand nand_10 (nand_10_out, nand_1_out, d_ff_2_q);
  nand nand_11 (nand_11_out, d_ff_3_q, X);
  nand nand_12 (nand_12_out, nand_2_out, d_ff_3_q);
  nand nand_13 (nand_13_out, nand_3_out, d_ff_2_q);
  nand nand_14 (nand_14_out, nand_4_out, X);
  nand nand_15 (nand_15_out, nand_5_out, nand_6_out);
  nand nand_16 (nand_16_out, nand_7_out, nand_8_out);
  nand nand_17 (nand_17_out, d_ff_1_q, nand_9_out);
  nand nand_18 (nand_18_out, nand_10_out, nand_10_out);
  nand nand_19 (nand_19_out, nand_11_out, nand_11_out);
  nand nand_20 (nand_20_out, nand_12_out, nand_12_out);
  nand nand_21 (nand_21_out, X, X);
  nand nand_22 (nand_22_out, nand_13_out, nand_13_out);
  nand nand_23 (nand_23_out, nand_14_out, nand_14_out);
  nand nand_24 (nand_24_out, d_ff_2_q, d_ff_2_q);
  nand nand_25 (nand_25_out, d_ff_3_q, d_ff_3_q);
  nand nand_26 (nand_26_out, X, X);
  nand nand_27 (nand_27_out, nand_15_out, nand_15_out);
  nand nand_28 (nand_28_out, nand_16_out, nand_16_out);
  nand nand_29 (nand_29_out, d_ff_2_q, d_ff_2_q);
  nand nand_30 (nand_30_out, d_ff_3_q, d_ff_3_q);
  nand nand_31 (nand_31_out, nand_17_out, nand_17_out);
  nand nand_32 (nand_32_out, d_ff_3_q, d_ff_3_q);
  nand nand_33 (nand_33_out, nand_18_out, nand_19_out);
  nand nand_34 (nand_34_out, nand_20_out, nand_21_out);
  nand nand_35 (nand_35_out, nand_22_out, nand_23_out);
  nand nand_36 (nand_36_out, d_ff_1_q, nand_24_out);
  nand nand_37 (nand_37_out, nand_25_out, nand_26_out);
  nand nand_38 (nand_38_out, nand_27_out, X);
  nand nand_39 (nand_39_out, nand_28_out, X);
  nand nand_40 (nand_40_out, nand_29_out, nand_30_out);
  nand nand_41 (nand_41_out, nand_31_out, nand_32_out);
  nand nand_42 (nand_42_out, nand_33_out, nand_33_out);
  nand nand_43 (nand_43_out, nand_34_out, nand_35_out);
  nand nand_44 (nand_44_out, nand_36_out, nand_36_out);
  nand nand_45 (nand_45_out, nand_37_out, nand_37_out);
  nand nand_46 (nand_46_out, nand_38_out, nand_39_out);
  nand nand_47 (nand_47_out, nand_40_out, nand_40_out);
  nand nand_48 (Z, nand_41_out, nand_41_out);
  nand nand_49 (nand_49_out, nand_43_out, nand_43_out);
  nand nand_50 (nand_50_out, nand_44_out, nand_45_out);
  nand nand_51 (nand_51_out, nand_46_out, nand_46_out);
  nand nand_52 (nand_52_out, nand_47_out, X);
  Clock clock_1 (.out(clock_1_out));
  nand nand_53 (nand_53_out, nand_49_out, nand_50_out);
  nand nand_54 (nand_54_out, nand_51_out, nand_52_out);
  D_Flip_Flop d_ff_1 (.clk(clock_1_out), .D(nand_42_out), .Q(d_ff_1_q));  // open: Qn, preset, en, reset
  D_Flip_Flop d_ff_2 (.clk(clock_1_out), .D(nand_53_out), .Q(d_ff_2_q));  // open: Qn, preset, en, reset
  D_Flip_Flop d_ff_3 (.clk(clock_1_out), .D(nand_54_out), .Q(d_ff_3_q));  // open: Qn, preset, en, reset
endmodule
