// Logisim project 5-Bit Arthimetic.circ as structural Verilog: 1 circuit, main circuit main
module main (
  input  A1,
  input  B1,
  input  A2,
  input  B2,
  input  A3,
  input  B3,
  input  A4,
  input  B4,
  input  A5,
  input  [3:0] in_10,
  input  M,
  input  B5,
  output [3:0] out_13,
  output out_14
);

  wire adder_2_cout, xor_5_out;
  wire [3:0] adder_1_out, xor_1_out, xor_6_out;

  Adder #(.width(4)) adder_1 (.a(in_10), .b(xor_1_out), .out(adder_1_out), .cin(A5));  // open: cout
  xor xor_1 (xor_1_out[0], A5, A1);
  xor xor_2 (xor_1_out[1], A5, A2);
  xor xor_3 (xor_1_out[2], A5, A3);
  xor xor_4 (xor_1_out[3], A4, A5);
  xor xor_5 (xor_5_out, M, B5);
  xor xor_6 (xor_6_out[0], xor_5_out, B1);
  xor xor_7 (xor_6_out[1], xor_5_out, B2);
  xor xor_8 (xor_6_out[2], xor_5_out, B3);
  xor xor_9 (xor_6_out[3], B4, xor_5_out);
  Adder #(.width(4)) adder_2 (.a(adder_1_out), .b(xor_6_out), .out(out_13), .cin(xor_5_out), .cout(adder_2_cout));
  ExactlyOne xor_10 (.out(out_14), .in0(adder_2_cout), .in1(xor_5_out), .in2(A5));
endmodule
