// Logisim project ALU.circ as structural Verilog: 1 circuit, main circuit main
module main (
  input  [2:0] Options,
  input  [3:0] A,
  input  [3:0] B,
  output [3:0] out_4
);

  wire [3:0] adder_1_out, and_1_out, multiplier_1_out, nor_1_out, or_1_out, xor_1_out;

  assign and_1_out = A & B;  // AND_Gate and_1, 4 bits wide
  assign or_1_out = A | B;  // OR_Gate or_1, 4 bits wide
  assign xor_1_out = A ^ B;  // XOR_Gate xor_1, 4 bits wide
  assign nor_1_out = ~(A | B);  // NOR_Gate nor_1, 4 bits wide
  Adder #(.width(4)) adder_1 (.a(A), .b(B), .out(adder_1_out));  // open: cin, cout
  Multiplier #(.width(4)) multiplier_1 (.a(A), .b(B), .out(multiplier_1_out));  // open: cin, cout
  Multiplexer #(.select(3), .width(4), .enable("false")) multiplexer_1 (
    .in0(and_1_out), .in1(or_1_out), .in2(xor_1_out), .in3(nor_1_out), .in4(adder_1_out),
    .in5(multiplier_1_out), .out(out_4), .sel(Options));  // open: in6, in7
endmodule
