// Logisim project DEC.circ as structural Verilog
module Disp (
);

  wire clock_1_out, nand_1_out, nand_2_out, nand_3_out, nand_4_out, nand_5_out, nand_6_out, nand_7_out,
       nand_8_out, nand_9_out, nand_10_out, nand_11_out, nand_12_out, nand_13_out, nand_14_out, nand_15_out,
       nand_16_out, nand_17_out, nand_18_out, nand_19_out, nand_20_out, nand_21_out, nand_22_out,
       nand_23_out, nand_24_out, nand_25_out, nand_26_out, nand_27_out, nand_28_out, nand_29_out,
       nand_30_out, nand_31_out, nand_32_out, nand_33_out, nand_34_out, nand_35_out, nand_36_out,
       nand_37_out, nand_38_out, nand_39_out, nand_40_out, nand_41_out, nand_42_out, nand_43_out,
       nand_44_out, nand_45_out, nand_46_out, nand_47_out, nand_48_out, nand_49_out, nand_50_out,
       nand_51_out, nand_52_out, nand_53_out, nand_54_out, nand_55_out, nand_56_out, nand_57_out,
       nand_58_out, nand_59_out, nand_60_out, nand_61_out, nand_62_out;
  wire [3:0] counter_1_q;

  Clock clock_1 (.out(clock_1_out));
  Counter #(.width(4), .max('h9)) counter_1 (
    .count(clock_1_out), .Q(counter_1_q), .clk(clock_1_out));  // open: load, D, carry, clr
  nand nand_1 (nand_1_out, counter_1_q[3], counter_1_q[3]);
  nand nand_2 (nand_2_out, counter_1_q[2], counter_1_q[2]);
  nand nand_3 (nand_3_out, counter_1_q[3], counter_1_q[3]);
  nand nand_4 (nand_4_out, counter_1_q[1], counter_1_q[1]);
  nand nand_5 (nand_5_out, counter_1_q[3], counter_1_q[3]);
  nand nand_6 (nand_6_out, counter_1_q[1], counter_1_q[1]);
  nand nand_7 (nand_7_out, counter_1_q[3], counter_1_q[3]);
  nand nand_8 (nand_8_out, counter_1_q[1], counter_1_q[1]);
  nand nand_9 (nand_9_out, counter_1_q[3], counter_1_q[3]);
  nand nand_10 (nand_10_out, counter_1_q[2], counter_1_q[2]);
  nand nand_11 (nand_11_out, counter_1_q[3], counter_1_q[3]);
  nand nand_12 (nand_12_out, counter_1_q[1], counter_1_q[1]);
  nand nand_13 (nand_13_out, counter_1_q[3], counter_1_q[3]);
  nand nand_14 (nand_14_out, counter_1_q[2], counter_1_q[2]);
  nand nand_15 (nand_15_out, counter_1_q[3], counter_1_q[3]);
  nand nand_16 (nand_16_out, counter_1_q[1], counter_1_q[1]);
  nand nand_17 (nand_17_out, counter_1_q[3], counter_1_q[3]);
  nand nand_18 (nand_18_out, counter_1_q[1], counter_1_q[1]);
  nand nand_19 (nand_19_out, counter_1_q[3], counter_1_q[3]);
  nand nand_20 (nand_20_out, nand_1_out, nand_2_out);
  nand nand_21 (nand_21_out, nand_3_out, nand_4_out);
  nand nand_22 (nand_22_out, nand_5_out, nand_6_out);
  nand nand_23 (nand_23_out, nand_7_out, nand_8_out);
  nand nand_24 (nand_24_out, nand_9_out, nand_10_out);
  nand nand_25 (nand_25_out, nand_11_out, nand_12_out);
  nand nand_26 (nand_26_out, nand_13_out, nand_14_out);
  nand nand_27 (nand_27_out, nand_15_out, nand_16_out);
  nand nand_28 (nand_28_out, nand_17_out, nand_18_out);
  nand nand_29 (nand_29_out, nand_19_out, counter_1_q[2]);
  nand nand_30 (nand_30_out, nand_20_out, nand_20_out);
  nand nand_31 (nand_31_out, counter_1_q[0], counter_1_q[0]);
  nand nand_32 (nand_32_out, counter_1_q[3], counter_1_q[3]);
  nand nand_33 (nand_33_out, counter_1_q[1], counter_1_q[1]);
  nand nand_34 (nand_34_out, nand_21_out, nand_21_out);
  nand nand_35 (nand_35_out, counter_1_q[0], counter_1_q[0]);
  nand nand_36 (nand_36_out, counter_1_q[1], counter_1_q[1]);
  nand nand_37 (nand_37_out, nand_22_out, nand_22_out);
  nand nand_38 (nand_38_out, counter_1_q[0], counter_1_q[0]);
  nand nand_39 (nand_39_out, counter_1_q[1], counter_1_q[1]);
  nand nand_40 (nand_40_out, counter_1_q[3], counter_1_q[3]);
  nand nand_41 (nand_41_out, counter_1_q[2], counter_1_q[2]);
  nand nand_42 (nand_42_out, nand_23_out, nand_23_out);
  nand nand_43 (nand_43_out, nand_24_out, nand_25_out);
  nand nand_44 (nand_44_out, nand_26_out, nand_27_out);
  nand nand_45 (nand_45_out, nand_28_out, nand_28_out);
  nand nand_46 (nand_46_out, nand_29_out, nand_29_out);
  nand nand_47 (nand_47_out, counter_1_q[1], counter_1_q[1]);
  nand nand_48 (nand_48_out, nand_30_out, nand_31_out);
  nand nand_49 (nand_49_out, nand_32_out, nand_33_out);
  nand nand_50 (nand_50_out, nand_34_out, nand_35_out);
  nand nand_51 (nand_51_out, counter_1_q[2], nand_36_out);
  nand nand_52 (nand_52_out, nand_37_out, nand_38_out);
  nand nand_53 (nand_53_out, counter_1_q[2], nand_39_out);
  nand nand_54 (nand_54_out, nand_40_out, nand_41_out);
  nand nand_55 (nand_55_out, nand_42_out, counter_1_q[0]);
  nand nand_56 (nand_56_out, nand_45_out, counter_1_q[0]);
  nand nand_57 (nand_57_out, nand_46_out, nand_47_out);
  nand nand_58 (nand_58_out, nand_48_out, nand_49_out);
  nand nand_59 (nand_59_out, nand_50_out, nand_51_out);
  nand nand_60 (nand_60_out, nand_52_out, nand_53_out);
  nand nand_61 (nand_61_out, nand_54_out, nand_55_out);
  nand nand_62 (nand_62_out, nand_56_out, nand_57_out);
  _7_Segment_Display u_7_segment_display_1 (
    .g(nand_62_out), .f(nand_44_out), .a(nand_58_out), .b(nand_59_out), .e(nand_43_out), .d(nand_61_out),
    .c(nand_60_out));  // open: dp
endmodule
