// Logisim project Johnson Counter.circ as structural Verilog: 1 circuit, main circuit main
module main (
  output out_1,
  output out_2,
  output out_3,
  output out_4,
  output out_5,
  output out_6
);

  wire clock_1_out, j_k_ff_1_q, j_k_ff_1_qn, j_k_ff_2_q, j_k_ff_2_qn, j_k_ff_3_q, j_k_ff_3_qn;

  Clock clock_1 (.out(clock_1_out));
  J_K_Flip_Flop j_k_ff_1 (
    .J(j_k_ff_3_qn), .clk(clock_1_out), .K(j_k_ff_3_q), .Q(j_k_ff_1_q), .Qn(j_k_ff_1_qn));  // open: preset, en, reset
  J_K_Flip_Flop j_k_ff_2 (
    .J(j_k_ff_1_q), .clk(clock_1_out), .K(j_k_ff_1_qn), .Q(j_k_ff_2_q), .Qn(j_k_ff_2_qn));  // open: preset, en, reset
  J_K_Flip_Flop j_k_ff_3 (
    .J(j_k_ff_2_q), .clk(clock_1_out), .K(j_k_ff_2_qn), .Q(j_k_ff_3_q), .Qn(j_k_ff_3_qn));  // open: preset, en, reset
  and and_1 (out_1, j_k_ff_3_qn, j_k_ff_1_qn);
  and and_2 (out_2, j_k_ff_1_q, j_k_ff_2_qn);
  and and_3 (out_3, j_k_ff_2_q, j_k_ff_3_qn);
  and and_4 (out_4, j_k_ff_1_q, j_k_ff_3_q);
  and and_5 (out_5, j_k_ff_2_q, j_k_ff_1_qn);
  and and_6 (out_6, j_k_ff_3_q, j_k_ff_2_qn);
endmodule
