// Logisim project Modulo-13(JKFF).circ as structural Verilog: 1 circuit, main circuit main
module main (
  output out_1,
  output out_2,
  output out_3,
  output out_4
);

  wire and_1_out, and_2_out, and_3_out, clock_1_out, not_1_out;

  Clock clock_1 (.out(clock_1_out));
  and and_1 (and_1_out, out_3, out_4);
  and and_2 (and_2_out, out_2, and_1_out);
  J_K_Flip_Flop j_k_ff_1 (.J(1'b1), .clk(clock_1_out), .K(1'b1), .Q(out_4), .reset(and_3_out));  // open: Qn, preset, en
  J_K_Flip_Flop j_k_ff_2 (
    .J(out_4), .clk(clock_1_out), .K(out_4), .Q(out_3), .reset(and_3_out));  // open: Qn, preset, en
  J_K_Flip_Flop j_k_ff_3 (
    .J(and_1_out), .clk(clock_1_out), .K(and_1_out), .Q(out_2), .reset(and_3_out));  // open: Qn, preset, en
  J_K_Flip_Flop j_k_ff_4 (
    .J(and_2_out), .clk(clock_1_out), .K(and_2_out), .Q(out_1), .reset(and_3_out));  // open: Qn, preset, en
  not not_1 (not_1_out, out_3);
  and and_3 (and_3_out, out_4, not_1_out, out_2, out_1);
endmodule
