// Logisim project Modulo-5(Sync).circ as structural Verilog
module Modulo_5_Sync (
  output DA,
  output DB,
  output DC,
  output out_4,
  output out_5,
  output out_6
);

  wire clock_1_out, nand_1_out, nand_2_out, nand_3_out, nand_4_out, nand_5_out, nand_6_out, nand_7_out,
       nand_8_out, nand_9_out, nand_10_out, nand_11_out;

  nand nand_1 (nand_1_out, out_4, out_4);
  nand nand_2 (nand_2_out, out_4, out_4);
  nand nand_3 (nand_3_out, out_5, out_5);
  nand nand_4 (nand_4_out, out_4, out_4);
  nand nand_5 (nand_5_out, out_6, out_6);
  nand nand_6 (nand_6_out, out_4, out_4);
  nand nand_7 (nand_7_out, out_6, out_6);
  nand nand_8 (nand_8_out, nand_1_out, out_5, out_6);
  nand nand_9 (nand_9_out, nand_2_out, nand_3_out, out_6);
  nand nand_10 (nand_10_out, nand_4_out, out_5, nand_5_out);
  nand nand_11 (nand_11_out, nand_6_out, nand_7_out);
  nand nand_12 (DA, nand_8_out, nand_8_out);
  nand nand_13 (DB, nand_9_out, nand_10_out);
  nand nand_14 (DC, nand_11_out, nand_11_out);
  Clock clock_1 (.out(clock_1_out));
  D_Flip_Flop d_ff_1 (.clk(clock_1_out), .D(DA), .Q(out_4));  // open: Qn, preset, en, reset
  D_Flip_Flop d_ff_2 (.clk(clock_1_out), .D(DB), .Q(out_5));  // open: Qn, preset, en, reset
  D_Flip_Flop d_ff_3 (.clk(clock_1_out), .D(DC), .Q(out_6));  // open: Qn, preset, en, reset
endmodule
