// Logisim project Modulo-8(Up&Down).circ as structural Verilog: 1 circuit, main circuit main
module main (
  input  M,
  output out_2,
  output out_3,
  output out_4
);

  wire clock_1_out, xor_1_out, xor_2_out;

  Clock clock_1 (.out(clock_1_out));
  xor xor_1 (xor_1_out, M, out_4);
  J_K_Flip_Flop j_k_ff_1 (.J(1'b1), .clk(clock_1_out), .K(1'b1), .Q(out_4));  // open: Qn, preset, en, reset
  J_K_Flip_Flop j_k_ff_2 (.J(1'b1), .clk(xor_1_out), .K(1'b1), .Q(out_3));  // open: Qn, preset, en, reset
  xor xor_2 (xor_2_out, M, out_3);
  J_K_Flip_Flop j_k_ff_3 (.J(1'b1), .clk(xor_2_out), .K(1'b1), .Q(out_2));  // open: Qn, preset, en, reset
endmodule
