// Logisim project Proj.circ as structural Verilog: 15 circuits, main circuit main
module main (
  input  in_1,
  input  Lift,
  input  Down
);

  wire _0_out, _1_out, _2_out, _3_out, _4_out, _5_out, _6_out, _7_out, _8_out, _9_out, and_1_out, and_2_out,
       and_3_out, count_1_out_3, disp_1_out_4, disp_1_out_5, disp_1_out_6, disp_1_out_7, disp_1_out_8,
       disp_1_out_9, disp_1_out_10, disp_1_out_11, disp_1_out_12, disp_1_out_13, disp_1_out_14,
       disp_1_out_15, disp_1_out_16, disp_1_out_17, disp_1_out_18, disp_1_out_19, disp_1_out_20,
       disp_1_out_21, disp_1_out_22, disp_1_out_23, disp_1_out_24, disp_1_out_25, disp_1_out_26,
       disp_1_out_27, disp_1_out_28, disp_1_out_29, disp_1_out_30, disp_1_out_31, disp_1_out_32,
       disp_1_out_33, disp_1_out_34, disp_1_out_35, disp_1_out_36, disp_1_out_37, disp_1_out_38,
       disp_1_out_39, disp_1_out_40, disp_1_out_41, disp_1_out_42, disp_1_out_43, disp_1_out_44,
       disp_1_out_45, disp_1_out_46, disp_1_out_47, disp_1_out_48, disp_1_out_49, disp_1_out_50,
       disp_1_out_51, disp_1_out_52, disp_1_out_53, disp_1_out_54, disp_1_out_55, disp_1_out_56,
       disp_1_out_57, disp_1_out_58, disp_1_out_59, disp_1_out_60, disp_1_out_61, disp_1_out_62,
       disp_1_out_63, disp_1_out_64, disp_1_out_65, disp_1_out_66, disp_1_out_67, disp_1_out_68,
       disp_1_out_69, disp_1_out_70, disp_1_out_71, disp_1_out_72, disp_1_out_73, disp_1_out_74,
       disp_1_out_75, disp_1_out_76, disp_1_out_77, disp_1_out_78, disp_1_out_79, disp_1_out_80, nand_1_out,
       nand_2_out, nand_3_out, nand_4_out, nand_5_out, not_1_out, not_6_out, not_7_out, not_8_out, not_9_out,
       not_10_out, not_11_out, not_12_out, not_13_out, not_14_out, not_15_out, not_16_out, not_17_out,
       not_18_out, not_19_out, not_20_out, or_1_out, or_3_out, or_4_out, or_5_out, or_6_out, or_7_out,
       or_8_out, or_9_out, or_10_out, or_11_out, or_12_out, or_13_out, or_14_out, or_15_out, or_16_out;
  wire [2:2] not_4_out, not_5_out;
  wire [3:0] counter_1_q, counter_2_q, counter_3_q, or_2_out, register_1_q, register_2_q, register_3_q,
       register_4_q, register_5_q, register_6_q, register_7_q, register_8_q, register_9_q, register_10_q,
       register_11_q, register_12_q, register_13_q, register_14_q, register_15_q, register_16_q,
       register_17_q, register_18_q, register_19_q, timer_1_out_2, timer_1_out_3, timer_1_out_4,
       timer_1_out_5;
  wire [3:3] not_2_out, not_3_out;

  or or_1 (or_1_out, Down, not_1_out);
  Disp disp_1 (
    .in_1(Lift), .in_2(in_1), .in_3(or_1_out), .out_4(disp_1_out_4), .out_5(disp_1_out_5),
    .out_6(disp_1_out_6), .out_7(disp_1_out_7), .out_8(disp_1_out_8), .out_9(disp_1_out_9),
    .out_10(disp_1_out_10), .out_11(disp_1_out_11), .out_12(disp_1_out_12), .out_13(disp_1_out_13),
    .out_14(disp_1_out_14), .out_15(disp_1_out_15), .out_16(disp_1_out_16), .out_17(disp_1_out_17),
    .out_18(disp_1_out_18), .out_19(disp_1_out_19), .out_20(disp_1_out_20), .out_21(disp_1_out_21),
    .out_22(disp_1_out_22), .out_23(disp_1_out_23), .out_24(disp_1_out_24), .out_25(disp_1_out_25),
    .out_26(disp_1_out_26), .out_27(disp_1_out_27), .out_28(disp_1_out_28), .out_29(disp_1_out_29),
    .out_30(disp_1_out_30), .out_31(disp_1_out_31), .out_32(disp_1_out_32), .out_33(disp_1_out_33),
    .out_34(disp_1_out_34), .out_35(disp_1_out_35), .out_36(disp_1_out_36), .out_37(disp_1_out_37),
    .out_38(disp_1_out_38), .out_39(disp_1_out_39), .out_40(disp_1_out_40), .out_41(disp_1_out_41),
    .out_42(disp_1_out_42), .out_43(disp_1_out_43), .out_44(disp_1_out_44), .out_45(disp_1_out_45),
    .out_46(disp_1_out_46), .out_47(disp_1_out_47), .out_48(disp_1_out_48), .out_49(disp_1_out_49),
    .out_50(disp_1_out_50), .out_51(disp_1_out_51), .out_52(disp_1_out_52), .out_53(disp_1_out_53),
    .out_54(disp_1_out_54), .out_55(disp_1_out_55), .out_56(disp_1_out_56), .out_57(disp_1_out_57),
    .out_58(disp_1_out_58), .out_59(disp_1_out_59), .out_60(disp_1_out_60), .out_61(disp_1_out_61),
    .out_62(disp_1_out_62), .out_63(disp_1_out_63), .out_64(disp_1_out_64), .out_65(disp_1_out_65),
    .out_66(disp_1_out_66), .out_67(disp_1_out_67), .out_68(disp_1_out_68), .out_69(disp_1_out_69),
    .out_70(disp_1_out_70), .out_71(disp_1_out_71), .out_72(disp_1_out_72), .out_73(disp_1_out_73),
    .out_74(disp_1_out_74), .out_75(disp_1_out_75), .out_76(disp_1_out_76), .out_77(disp_1_out_77),
    .out_78(disp_1_out_78), .out_79(disp_1_out_79), .out_80(disp_1_out_80));
  not not_1 (not_1_out, or_16_out);
  Hex_Digit_Display hex_digit_display_1 (.value(counter_3_q));  // open: dp
  Hex_Digit_Display hex_digit_display_2 (.value(counter_2_q));  // open: dp
  Button _9 (.out(_9_out));
  Button _8 (.out(_8_out));
  Button _7 (.out(_7_out));
  Button _6 (.out(_6_out));
  Button _5 (.out(_5_out));
  Button _4 (.out(_4_out));
  Button _3 (.out(_3_out));
  Button _2 (.out(_2_out));
  Button _1 (.out(_1_out));
  Button _0 (.out(_0_out));
  _7_Segment_Display u_7_segment_display_1 (
    .g(disp_1_out_10), .f(disp_1_out_9), .a(disp_1_out_4), .b(disp_1_out_5), .e(disp_1_out_8),
    .d(disp_1_out_7), .c(disp_1_out_6));  // open: dp
  Hex_Digit_Display hex_digit_display_3 (.value(register_2_q));  // open: dp
  not not_2 (not_2_out[3], 1'b1);
  not not_3 (not_3_out[3], 1'b1);
  not not_4 (not_4_out[2], 1'b1);
  not not_5 (not_5_out[2], 1'b1);
  _7_Segment_Display u_7_segment_display_2 (
    .g(disp_1_out_17), .f(disp_1_out_16), .a(disp_1_out_11), .b(disp_1_out_12), .e(disp_1_out_15),
    .d(disp_1_out_14), .c(disp_1_out_13));  // open: dp
  _7_Segment_Display u_7_segment_display_3 (
    .g(disp_1_out_24), .f(disp_1_out_23), .a(disp_1_out_18), .b(disp_1_out_19), .e(disp_1_out_22),
    .d(disp_1_out_21), .c(disp_1_out_20));  // open: dp
  Hex_Digit_Display hex_digit_display_4 (.value(register_1_q));  // open: dp
  Hex_Digit_Display hex_digit_display_5 (.value(register_13_q));  // open: dp
  Register #(.width(4)) register_1 (.D(register_13_q), .Q(register_1_q), .clk(and_1_out));  // open: en, clr
  Register #(.width(4)) register_2 (.D(register_1_q), .Q(register_2_q), .clk(and_1_out));  // open: en, clr
  Register #(.width(4)) register_3 (.D({4{not_2_out[3]}}), .Q(register_3_q), .clk(_0_out), .clr(or_4_out));  // open: en
  Register #(.width(4)) register_4 (
    .D({{3{not_2_out[3]}}, 1'b1}), .Q(register_4_q), .clk(_1_out), .clr(or_5_out));  // open: en
  Register #(.width(4)) register_5 (
    .D({{2{not_2_out[3]}}, 1'b1, not_2_out[3]}), .Q(register_5_q), .clk(_2_out), .clr(or_6_out));  // open: en
  Register #(.width(4)) register_6 (
    .D({{2{not_2_out[3]}}, 2'b11}), .Q(register_6_q), .clk(_3_out), .clr(or_7_out));  // open: en
  Register #(.width(4)) register_7 (
    .D({not_2_out[3], 1'b1, {2{not_2_out[3]}}}), .Q(register_7_q), .clk(_4_out), .clr(or_13_out));  // open: en
  Register #(.width(4)) register_8 (
    .D({not_2_out[3], 1'b1, not_2_out[3], 1'b1}), .Q(register_8_q), .clk(_5_out), .clr(or_8_out));  // open: en
  Register #(.width(4)) register_9 (
    .D({not_2_out[3], 2'b11, not_2_out[3]}), .Q(register_9_q), .clk(_6_out), .clr(or_9_out));  // open: en
  Register #(.width(4)) register_10 (
    .D({not_3_out[3], 3'b111}), .Q(register_10_q), .clk(_7_out), .clr(or_10_out));  // open: en
  Register #(.width(4)) register_11 (
    .D({1'b1, {3{not_4_out[2]}}}), .Q(register_11_q), .clk(_8_out), .clr(or_11_out));  // open: en
  Register #(.width(4)) register_12 (
    .D({1'b1, {2{not_5_out[2]}}, 1'b1}), .Q(register_12_q), .clk(_9_out), .clr(or_12_out));  // open: en
  _7_Segment_Display u_7_segment_display_4 (
    .g(disp_1_out_38), .f(disp_1_out_37), .a(disp_1_out_32), .b(disp_1_out_33), .e(disp_1_out_36),
    .d(disp_1_out_35), .c(disp_1_out_34));  // open: dp
  _7_Segment_Display u_7_segment_display_5 (
    .g(disp_1_out_31), .f(disp_1_out_30), .a(disp_1_out_25), .b(disp_1_out_26), .e(disp_1_out_29),
    .d(disp_1_out_28), .c(disp_1_out_27));  // open: dp
  Hex_Digit_Display hex_digit_display_6 (.value(register_16_q));  // open: dp
  Hex_Digit_Display hex_digit_display_7 (.value(register_14_q));  // open: dp
  Register #(.width(4)) register_13 (.D(register_14_q), .Q(register_13_q), .clk(and_1_out));  // open: en, clr
  _7_Segment_Display u_7_segment_display_6 (
    .g(disp_1_out_45), .f(disp_1_out_44), .a(disp_1_out_39), .b(disp_1_out_40), .e(disp_1_out_43),
    .d(disp_1_out_42), .c(disp_1_out_41));  // open: dp
  _7_Segment_Display u_7_segment_display_7 (
    .g(disp_1_out_52), .f(disp_1_out_51), .a(disp_1_out_46), .b(disp_1_out_47), .e(disp_1_out_50),
    .d(disp_1_out_49), .c(disp_1_out_48));  // open: dp
  Hex_Digit_Display hex_digit_display_8 (.value(register_17_q));  // open: dp
  Hex_Digit_Display hex_digit_display_9 (.value(register_15_q));  // open: dp
  Register #(.width(4)) register_14 (.D(register_16_q), .Q(register_14_q), .clk(and_1_out));  // open: en, clr
  _7_Segment_Display u_7_segment_display_8 (
    .g(disp_1_out_66), .f(disp_1_out_65), .a(disp_1_out_60), .b(disp_1_out_61), .e(disp_1_out_64),
    .d(disp_1_out_63), .c(disp_1_out_62));  // open: dp
  _7_Segment_Display u_7_segment_display_9 (
    .g(disp_1_out_59), .f(disp_1_out_58), .a(disp_1_out_53), .b(disp_1_out_54), .e(disp_1_out_57),
    .d(disp_1_out_56), .c(disp_1_out_55));  // open: dp
  Hex_Digit_Display hex_digit_display_10 (.value(register_18_q));  // open: dp
  Hex_Digit_Display hex_digit_display_11 (.value(register_19_q));  // open: dp
  Register #(.width(4)) register_15 (.D(register_17_q), .Q(register_15_q), .clk(and_1_out));  // open: en, clr
  Register #(.width(4)) register_16 (.D(register_15_q), .Q(register_16_q), .clk(and_1_out));  // open: en, clr
  Register #(.width(4)) register_17 (.D(register_18_q), .Q(register_17_q), .clk(and_1_out));  // open: en, clr
  _7_Segment_Display u_7_segment_display_10 (
    .g(disp_1_out_80), .f(disp_1_out_79), .a(disp_1_out_74), .b(disp_1_out_75), .e(disp_1_out_78),
    .d(disp_1_out_77), .c(disp_1_out_76));  // open: dp
  _7_Segment_Display u_7_segment_display_11 (
    .g(disp_1_out_73), .f(disp_1_out_72), .a(disp_1_out_67), .b(disp_1_out_68), .e(disp_1_out_71),
    .d(disp_1_out_70), .c(disp_1_out_69));  // open: dp
  Hex_Digit_Display hex_digit_display_12 (.value(or_2_out));  // open: dp
  not not_6 (not_6_out, Down);
  Register #(.width(4)) register_18 (.D(register_19_q), .Q(register_18_q), .clk(and_1_out));  // open: en, clr
  Register #(.width(4)) register_19 (.D(or_2_out), .Q(register_19_q), .clk(and_1_out));  // open: en, clr
  and and_1 (and_1_out, not_7_out, or_3_out);
  assign or_2_out = register_3_q | register_4_q | register_5_q | register_6_q | register_7_q | register_8_q | register_9_q | register_10_q | register_11_q | register_12_q;  // OR_Gate or_2, 4 bits wide
  Hex_Digit_Display hex_digit_display_13 (.value(timer_1_out_2));  // open: dp
  Hex_Digit_Display hex_digit_display_14 (.value(timer_1_out_3));  // open: dp
  and and_2 (and_2_out, not_6_out, and_3_out);
  not not_7 (not_7_out, and_3_out);
  or or_3 (or_3_out, _9_out, _8_out, _7_out, _6_out, _5_out, _4_out, _3_out, _2_out, _1_out, _0_out);
  Hex_Digit_Display hex_digit_display_15 (.value(timer_1_out_4));  // open: dp
  Counter #(.width(4), .max('ha), .ongoal("stay")) counter_1 (
    .Q(counter_1_q), .clk(or_3_out));  // open: load, D, count, carry, clr
  Hex_Digit_Display hex_digit_display_16 (.value(timer_1_out_5));  // open: dp
  Counter #(.width(4), .max('h6), .ongoal("stay")) counter_2 (
    .count(nand_5_out), .Q(counter_2_q), .clk(nand_5_out));  // open: load, D, carry, clr
  not not_8 (not_8_out, Down);
  Count count_1 (.in_1(timer_1_out_4), .in_2(timer_1_out_5), .out_3(count_1_out_3));
  Timer timer_1 (
    .in_1(and_2_out), .out_2(timer_1_out_2), .out_3(timer_1_out_3), .out_4(timer_1_out_4),
    .out_5(timer_1_out_5));
  not not_9 (not_9_out, timer_1_out_2[1]);
  not not_10 (not_10_out, timer_1_out_2[3]);
  not not_11 (not_11_out, timer_1_out_3[1]);
  not not_12 (not_12_out, timer_1_out_4[1]);
  not not_13 (not_13_out, timer_1_out_4[3]);
  not not_14 (not_14_out, timer_1_out_5[1]);
  or or_4 (or_4_out, _1_out, _2_out, _3_out, _4_out, _5_out, _6_out, _7_out, _8_out, _9_out);
  or or_5 (or_5_out, _0_out, _2_out, _3_out, _4_out, _5_out, _6_out, _7_out, _8_out, _9_out);
  or or_6 (or_6_out, _0_out, _1_out, _3_out, _4_out, _5_out, _6_out, _7_out, _8_out, _9_out);
  or or_7 (or_7_out, _0_out, _1_out, _2_out, _4_out, _5_out, _6_out, _7_out, _8_out, _9_out);
  or or_8 (or_8_out, _0_out, _1_out, _2_out, _3_out, _4_out, _6_out, _7_out, _8_out, _9_out);
  or or_9 (or_9_out, _0_out, _1_out, _2_out, _3_out, _4_out, _5_out, _7_out, _8_out, _9_out);
  or or_10 (or_10_out, _0_out, _1_out, _2_out, _3_out, _4_out, _5_out, _6_out, _8_out, _9_out);
  or or_11 (or_11_out, _0_out, _1_out, _2_out, _3_out, _4_out, _5_out, _6_out, _7_out, _9_out);
  or or_12 (or_12_out, _0_out, _1_out, _2_out, _3_out, _4_out, _5_out, _6_out, _7_out, _8_out);
  or or_13 (or_13_out, _0_out, _1_out, _2_out, _3_out, _5_out, _6_out, _7_out, _8_out, _9_out);
  not not_15 (not_15_out, counter_1_q[0]);
  not not_16 (not_16_out, counter_1_q[2]);
  Counter #(.width(4), .max('h9)) counter_3 (
    .count(not_8_out), .Q(counter_3_q), .clk(count_1_out_3));  // open: load, D, carry, clr
  not not_17 (not_17_out, timer_1_out_3[2]);
  nand nand_1 (nand_1_out, timer_1_out_4[0], not_12_out, timer_1_out_4[2], not_13_out);
  not not_18 (not_18_out, timer_1_out_5[2]);
  and and_3 (and_3_out, not_15_out, counter_1_q[1], not_16_out, counter_1_q[3]);
  not not_19 (not_19_out, counter_3_q[1]);
  not not_20 (not_20_out, counter_3_q[2]);
  nand nand_2 (nand_2_out, timer_1_out_2[0], not_9_out, timer_1_out_2[2], not_10_out);
  nand nand_3 (nand_3_out, timer_1_out_3[0], not_11_out, not_17_out, timer_1_out_3[3]);
  nand nand_4 (nand_4_out, timer_1_out_5[0], not_14_out, not_18_out, timer_1_out_5[3]);
  nand nand_5 (nand_5_out, counter_3_q[0], not_19_out, not_20_out, counter_3_q[3]);
  or or_14 (or_14_out, nand_2_out, nand_3_out);
  or or_15 (or_15_out, nand_1_out, nand_4_out);
  or or_16 (or_16_out, or_14_out, or_15_out);

  // Notes on the sheet:
  //   Cost
  //   DIsplay
  //   PUBLIC TELEPHONE
  //   Time
endmodule

module _1 (
  input  Lift,
  input  Coin,
  input  Down,
  output a,
  output b,
  output c,
  output d,
  output e,
  output f,
  output g
);

  wire not_1_out, not_2_out;

  not not_1 (not_1_out, Down);
  not not_2 (not_2_out, Down);
  and and_1 (d, Lift, Coin);
  and and_2 (e, Lift, Coin);
  and and_3 (f, Lift, Coin, Down);
  and and_4 (g, Lift, Coin);
  and and_5 (b, Lift, not_1_out);
  and and_6 (c, Lift, not_2_out);

  assign a = 1'b0;
endmodule

module _2 (
  input  Lift,
  input  Coin,
  input  Down,
  output a,
  output b,
  output c,
  output d,
  output e,
  output f,
  output g
);

  wire and_4_out, and_5_out, and_6_out, and_7_out, and_8_out, and_9_out, not_1_out, not_2_out, not_3_out,
       not_4_out, not_5_out, not_6_out, not_7_out, not_8_out;

  not not_1 (not_1_out, Coin);
  not not_2 (not_2_out, Down);
  not not_3 (not_3_out, Down);
  not not_4 (not_4_out, Down);
  not not_5 (not_5_out, Coin);
  not not_6 (not_6_out, Down);
  not not_7 (not_7_out, Coin);
  not not_8 (not_8_out, Down);
  and and_1 (g, Lift, Coin, Down);
  and and_2 (a, Lift, not_1_out, not_2_out);
  and and_3 (b, Lift, not_3_out);
  and and_4 (and_4_out, Lift, not_4_out);
  and and_5 (and_5_out, Lift, Coin);
  and and_6 (and_6_out, Lift, not_5_out, not_6_out);
  and and_7 (and_7_out, Lift, Coin, Down);
  and and_8 (and_8_out, Lift, not_7_out, not_8_out);
  and and_9 (and_9_out, Lift, Coin, Down);
  or or_1 (c, and_4_out, and_5_out);
  or or_2 (e, and_6_out, and_7_out);
  or or_3 (f, and_8_out, and_9_out);

  assign d = 1'b0;
endmodule

module _3 (
  input  Lift,
  input  Coin,
  input  Down,
  output a,
  output b,
  output c,
  output d,
  output e,
  output f,
  output g
);

  wire and_3_out, and_4_out, and_5_out, and_6_out, and_7_out, and_8_out, and_10_out, and_11_out, not_1_out,
       not_2_out, not_3_out, not_4_out, not_5_out, not_6_out;

  not not_1 (not_1_out, Down);
  and and_1 (b, Lift, Coin);
  not not_2 (not_2_out, Down);
  not not_3 (not_3_out, Down);
  and and_2 (e, Lift, Coin);
  not not_4 (not_4_out, Coin);
  not not_5 (not_5_out, Down);
  not not_6 (not_6_out, Down);
  and and_3 (and_3_out, Lift, not_1_out);
  and and_4 (and_4_out, Lift, Coin);
  and and_5 (and_5_out, Lift, not_2_out);
  and and_6 (and_6_out, Lift, Coin);
  and and_7 (and_7_out, Lift, not_3_out);
  and and_8 (and_8_out, Lift, Coin);
  and and_9 (f, Lift, not_4_out, not_5_out);
  and and_10 (and_10_out, Lift, not_6_out);
  and and_11 (and_11_out, Lift, Coin);
  or or_1 (a, and_3_out, and_4_out);
  or or_2 (c, and_5_out, and_6_out);
  or or_3 (d, and_7_out, and_8_out);
  or or_4 (g, and_10_out, and_11_out);
endmodule

module _4 (
  input  Lift,
  input  Coin,
  input  Down,
  output a,
  output b,
  output c,
  output d,
  output e,
  output f,
  output g
);

  wire and_2_out, and_3_out, and_4_out, and_5_out, and_7_out, and_8_out, and_9_out, and_10_out, not_1_out,
       not_2_out, not_3_out, not_4_out, not_5_out, not_6_out, not_7_out, not_8_out, not_9_out;

  not not_1 (not_1_out, Coin);
  not not_2 (not_2_out, Down);
  not not_3 (not_3_out, Coin);
  not not_4 (not_4_out, Down);
  and and_1 (c, Lift, Coin, Down);
  not not_5 (not_5_out, Down);
  not not_6 (not_6_out, Down);
  not not_7 (not_7_out, Down);
  not not_8 (not_8_out, Coin);
  not not_9 (not_9_out, Down);
  and and_2 (and_2_out, Lift, not_1_out, not_2_out);
  and and_3 (and_3_out, Lift, Coin, Down);
  and and_4 (and_4_out, Lift, not_3_out, not_4_out);
  and and_5 (and_5_out, Lift, Coin, Down);
  and and_6 (d, Lift, not_5_out);
  and and_7 (and_7_out, Lift, not_6_out);
  and and_8 (and_8_out, Lift, Coin);
  and and_9 (and_9_out, Lift, not_7_out);
  and and_10 (and_10_out, Lift, Coin);
  and and_11 (g, Lift, not_8_out, not_9_out);
  or or_1 (a, and_2_out, and_3_out);
  or or_2 (b, and_4_out, and_5_out);
  or or_3 (e, and_7_out, and_8_out);
  or or_4 (f, and_9_out, and_10_out);
endmodule

module _5 (
  input  Lift,
  input  Coin,
  input  Down,
  output a,
  output b,
  output c,
  output d,
  output e,
  output f,
  output g
);

  wire and_4_out, and_5_out, and_7_out, and_8_out, not_1_out, not_2_out, not_3_out, not_4_out, not_5_out,
       not_6_out;

  not not_1 (not_1_out, Coin);
  not not_2 (not_2_out, Down);
  and and_1 (b, Lift, Coin, Down);
  and and_2 (c, Lift, Coin, Down);
  not not_3 (not_3_out, Coin);
  not not_4 (not_4_out, Down);
  not not_5 (not_5_out, Coin);
  not not_6 (not_6_out, Down);
  and and_3 (g, Lift, Coin, Down);
  and and_4 (and_4_out, Lift, not_1_out, not_2_out);
  and and_5 (and_5_out, Lift, Coin, Down);
  and and_6 (e, Lift, not_3_out, not_4_out);
  and and_7 (and_7_out, Lift, not_5_out, not_6_out);
  and and_8 (and_8_out, Lift, Coin, Down);
  or or_1 (a, and_4_out, and_5_out);
  or or_2 (f, and_7_out, and_8_out);

  assign d = 1'b0;
endmodule

module _6 (
  input  Lift,
  input  Coin,
  input  Down,
  output a,
  output b,
  output c,
  output d,
  output e,
  output f,
  output g
);

  wire not_1_out, not_2_out, not_3_out, not_4_out, not_5_out, not_6_out, not_7_out, not_8_out, not_9_out;

  not not_1 (not_1_out, Down);
  not not_2 (not_2_out, Down);
  not not_3 (not_3_out, Down);
  not not_4 (not_4_out, Coin);
  not not_5 (not_5_out, Down);
  not not_6 (not_6_out, Down);
  not not_7 (not_7_out, Down);
  not not_8 (not_8_out, Coin);
  not not_9 (not_9_out, Down);
  and and_1 (a, Lift, Coin, not_1_out);
  and and_2 (b, Lift, Coin, not_2_out);
  and and_3 (c, Lift, Coin, not_3_out);
  and and_4 (d, Lift, not_4_out, not_5_out);
  and and_5 (e, Lift, not_6_out);
  and and_6 (f, Lift, not_7_out);
  and and_7 (g, Lift, not_8_out, not_9_out);
endmodule

module _7 (
  input  Lift,
  input  Coin,
  input  Down,
  output a,
  output b,
  output c,
  output d,
  output e,
  output f,
  output g
);

  wire not_1_out, not_2_out, not_3_out, not_4_out, not_5_out, not_6_out;

  not not_1 (not_1_out, Down);
  not not_2 (not_2_out, Down);
  not not_3 (not_3_out, Down);
  not not_4 (not_4_out, Down);
  not not_5 (not_5_out, Down);
  not not_6 (not_6_out, Down);
  and and_1 (a, Lift, Coin, not_1_out);
  and and_2 (b, Lift, Coin, not_2_out);
  and and_3 (c, Lift, Coin, not_3_out);
  and and_4 (d, Lift, Coin, not_4_out);
  and and_5 (e, Lift, Coin, not_5_out);
  and and_6 (f, Lift, Coin, not_6_out);

  assign g = 1'b0;
endmodule

module _8 (
  input  Lift,
  input  Coin,
  input  Down,
  output a,
  output b,
  output c,
  output d,
  output e,
  output f,
  output g
);

  wire not_1_out, not_2_out, not_3_out, not_4_out, not_5_out, not_6_out, not_7_out, not_8_out;

  not not_1 (not_1_out, Coin);
  not not_2 (not_2_out, Down);
  not not_3 (not_3_out, Coin);
  not not_4 (not_4_out, Down);
  not not_5 (not_5_out, Coin);
  not not_6 (not_6_out, Down);
  not not_7 (not_7_out, Coin);
  not not_8 (not_8_out, Down);
  and and_1 (a, Lift, not_1_out, not_2_out);
  and and_2 (d, Lift, not_3_out, not_4_out);
  and and_3 (e, Lift, not_5_out, not_6_out);
  and and_4 (f, Lift, not_7_out, not_8_out);

  assign b = 1'b0;
  assign c = 1'b0;
  assign g = 1'b0;
endmodule

module _9 (
  input  Lift,
  input  Coin,
  input  Down,
  output a,
  output b,
  output c,
  output d,
  output e,
  output f,
  output g
);

  wire not_1_out, not_2_out, not_3_out, not_4_out, not_5_out, not_6_out, not_7_out, not_8_out, not_9_out,
       not_10_out, not_11_out, not_12_out;

  not not_1 (not_1_out, Coin);
  not not_2 (not_2_out, Down);
  not not_3 (not_3_out, Coin);
  not not_4 (not_4_out, Down);
  not not_5 (not_5_out, Coin);
  not not_6 (not_6_out, Down);
  not not_7 (not_7_out, Coin);
  not not_8 (not_8_out, Down);
  not not_9 (not_9_out, Coin);
  not not_10 (not_10_out, Down);
  not not_11 (not_11_out, Coin);
  not not_12 (not_12_out, Down);
  and and_1 (a, Lift, not_1_out, not_2_out);
  and and_2 (b, Lift, not_3_out, not_4_out);
  and and_3 (c, Lift, not_5_out, not_6_out);
  and and_4 (d, Lift, not_7_out, not_8_out);
  and and_5 (e, Lift, not_9_out, not_10_out);
  and and_6 (f, Lift, not_11_out, not_12_out);

  assign g = 1'b0;
endmodule

module _10 (
  input  Lift,
  input  Coin,
  input  Down,
  output a,
  output b,
  output c,
  output d,
  output e,
  output f,
  output g
);

  wire not_1_out, not_2_out, not_3_out, not_4_out;

  not not_1 (not_1_out, Coin);
  not not_2 (not_2_out, Down);
  not not_3 (not_3_out, Coin);
  not not_4 (not_4_out, Down);
  and and_1 (b, Lift, not_1_out, not_2_out);
  and and_2 (c, Lift, not_3_out, not_4_out);

  assign a = 1'b0;
  assign d = 1'b0;
  assign e = 1'b0;
  assign f = 1'b0;
  assign g = 1'b0;
endmodule

module _11 (
  input  Lift,
  input  Coin,
  input  Down,
  output a,
  output b,
  output c,
  output d,
  output e,
  output f,
  output g
);

  wire not_1_out, not_2_out, not_3_out, not_4_out, not_5_out, not_6_out, not_7_out, not_8_out, not_9_out,
       not_10_out;

  not not_1 (not_1_out, Coin);
  not not_2 (not_2_out, Down);
  not not_3 (not_3_out, Coin);
  not not_4 (not_4_out, Down);
  not not_5 (not_5_out, Coin);
  not not_6 (not_6_out, Down);
  not not_7 (not_7_out, Coin);
  not not_8 (not_8_out, Down);
  not not_9 (not_9_out, Coin);
  not not_10 (not_10_out, Down);
  and and_1 (a, Lift, not_1_out, not_2_out);
  and and_2 (b, Lift, not_3_out, not_4_out);
  and and_3 (c, Lift, not_5_out, not_6_out);
  and and_4 (e, Lift, not_7_out, not_8_out);
  and and_5 (f, Lift, not_9_out, not_10_out);

  assign d = 1'b0;
  assign g = 1'b0;
endmodule

module Disp (
  input  in_1,
  input  in_2,
  input  in_3,
  output out_4,
  output out_5,
  output out_6,
  output out_7,
  output out_8,
  output out_9,
  output out_10,
  output out_11,
  output out_12,
  output out_13,
  output out_14,
  output out_15,
  output out_16,
  output out_17,
  output out_18,
  output out_19,
  output out_20,
  output out_21,
  output out_22,
  output out_23,
  output out_24,
  output out_25,
  output out_26,
  output out_27,
  output out_28,
  output out_29,
  output out_30,
  output out_31,
  output out_32,
  output out_33,
  output out_34,
  output out_35,
  output out_36,
  output out_37,
  output out_38,
  output out_39,
  output out_40,
  output out_41,
  output out_42,
  output out_43,
  output out_44,
  output out_45,
  output out_46,
  output out_47,
  output out_48,
  output out_49,
  output out_50,
  output out_51,
  output out_52,
  output out_53,
  output out_54,
  output out_55,
  output out_56,
  output out_57,
  output out_58,
  output out_59,
  output out_60,
  output out_61,
  output out_62,
  output out_63,
  output out_64,
  output out_65,
  output out_66,
  output out_67,
  output out_68,
  output out_69,
  output out_70,
  output out_71,
  output out_72,
  output out_73,
  output out_74,
  output out_75,
  output out_76,
  output out_77,
  output out_78,
  output out_79,
  output out_80
);

  _1 u_1_1 (
    .Lift(in_1), .Coin(in_2), .Down(in_3), .a(out_4), .b(out_5), .c(out_6), .d(out_7), .e(out_8), .f(out_9),
    .g(out_10));
  _2 u_2_1 (
    .Lift(in_1), .Coin(in_2), .Down(in_3), .a(out_11), .b(out_12), .c(out_13), .d(out_14), .e(out_15),
    .f(out_16), .g(out_17));
  _3 u_3_1 (
    .Lift(in_1), .Coin(in_2), .Down(in_3), .a(out_18), .b(out_19), .c(out_20), .d(out_21), .e(out_22),
    .f(out_23), .g(out_24));
  _4 u_4_1 (
    .Lift(in_1), .Coin(in_2), .Down(in_3), .a(out_25), .b(out_26), .c(out_27), .d(out_28), .e(out_29),
    .f(out_30), .g(out_31));
  _5 u_5_1 (
    .Lift(in_1), .Coin(in_2), .Down(in_3), .a(out_32), .b(out_33), .c(out_34), .d(out_35), .e(out_36),
    .f(out_37), .g(out_38));
  _6 u_6_1 (
    .Lift(in_1), .Coin(in_2), .Down(in_3), .a(out_39), .b(out_40), .c(out_41), .d(out_42), .e(out_43),
    .f(out_44), .g(out_45));
  _7 u_7_1 (
    .Lift(in_1), .Coin(in_2), .Down(in_3), .a(out_46), .b(out_47), .c(out_48), .d(out_49), .e(out_50),
    .f(out_51), .g(out_52));
  _8 u_8_1 (
    .Lift(in_1), .Coin(in_2), .Down(in_3), .a(out_53), .b(out_54), .c(out_55), .d(out_56), .e(out_57),
    .f(out_58), .g(out_59));
  _9 u_9_1 (
    .Lift(in_1), .Coin(in_2), .Down(in_3), .a(out_60), .b(out_61), .c(out_62), .d(out_63), .e(out_64),
    .f(out_65), .g(out_66));
  _10 u_10_1 (
    .Lift(in_1), .Coin(in_2), .Down(in_3), .a(out_67), .b(out_68), .c(out_69), .d(out_70), .e(out_71),
    .f(out_72), .g(out_73));
  _11 u_11_1 (
    .Lift(in_1), .Coin(in_2), .Down(in_3), .a(out_74), .b(out_75), .c(out_76), .d(out_77), .e(out_78),
    .f(out_79), .g(out_80));
endmodule

module Timer (
  input  in_1,
  output [3:0] out_2,
  output [3:0] out_3,
  output [3:0] out_4,
  output [3:0] out_5
);

  wire and_1_out, clock_1_out, nand_1_out, nand_2_out, nand_3_out, nand_4_out, not_1_out, not_2_out,
       not_3_out, not_4_out, not_5_out, not_6_out, not_7_out, not_8_out, or_1_out, or_2_out, or_3_out;

  Clock clock_1 (.out(clock_1_out));
  and and_1 (and_1_out, in_1, or_3_out);
  Counter #(.width(4), .max('h5), .ongoal("stay")) counter_1 (
    .count(nand_3_out), .Q(out_2), .clk(nand_3_out));  // open: load, D, carry, clr
  Counter #(.width(4), .max('h9)) counter_2 (.count(or_2_out), .Q(out_3), .clk(or_2_out));  // open: load, D, carry, clr
  Counter #(.width(4), .max('h5)) counter_3 (
    .count(nand_4_out), .Q(out_4), .clk(nand_4_out));  // open: load, D, carry, clr
  Counter #(.width(4), .max('h9)) counter_4 (
    .count(and_1_out), .Q(out_5), .clk(clock_1_out));  // open: load, D, carry, clr
  not not_1 (not_1_out, out_2[1]);
  not not_2 (not_2_out, out_2[3]);
  not not_3 (not_3_out, out_3[1]);
  not not_4 (not_4_out, out_4[1]);
  not not_5 (not_5_out, out_4[3]);
  not not_6 (not_6_out, out_5[1]);
  not not_7 (not_7_out, out_3[2]);
  nand nand_1 (nand_1_out, out_4[0], not_4_out, out_4[2], not_5_out);
  not not_8 (not_8_out, out_5[2]);
  nand nand_2 (nand_2_out, out_2[0], not_1_out, out_2[2], not_2_out);
  nand nand_3 (nand_3_out, out_3[0], not_3_out, not_7_out, out_3[3]);
  nand nand_4 (nand_4_out, out_5[0], not_6_out, not_8_out, out_5[3]);
  or or_1 (or_1_out, nand_2_out, nand_3_out);
  or or_2 (or_2_out, nand_1_out, nand_4_out);
  or or_3 (or_3_out, or_1_out, or_2_out);
endmodule

module Count (
  input  [3:0] in_1,
  input  [3:0] in_2,
  output out_3
);

  wire nand_1_out, nand_2_out, not_1_out, not_2_out, not_3_out, not_4_out, not_5_out, not_6_out, not_7_out;

  not not_1 (not_1_out, in_1[0]);
  not not_2 (not_2_out, in_1[1]);
  not not_3 (not_3_out, in_1[2]);
  not not_4 (not_4_out, in_1[3]);
  not not_5 (not_5_out, in_2[1]);
  not not_6 (not_6_out, in_2[2]);
  not not_7 (not_7_out, in_2[3]);
  nand nand_1 (nand_1_out, not_1_out, not_2_out, not_3_out, not_4_out);
  nand nand_2 (nand_2_out, in_2[0], not_5_out, not_6_out, not_7_out);
  or or_1 (out_3, nand_1_out, nand_2_out);
endmodule
