// Logisim project Seq-Gen.circ as structural Verilog
module Seq_Gen (
  output DA,
  output DB,
  output DC,
  output Z
);

  wire clock_1_out, d_ff_3_q, nand_1_out, nand_2_out, nand_3_out, nand_4_out, nand_5_out, nand_6_out,
       nand_7_out, nand_8_out, nand_9_out, nand_10_out, nand_11_out, nand_12_out, nand_13_out, nand_14_out,
       nand_15_out, nand_16_out, nand_17_out, nand_19_out, nand_20_out;

  nand nand_1 (nand_1_out, DB, DB);
  nand nand_2 (nand_2_out, DB, DB);
  nand nand_3 (nand_3_out, DC, DC);
  nand nand_4 (nand_4_out, nand_1_out, DC);
  nand nand_5 (nand_5_out, nand_2_out, d_ff_3_q);
  nand nand_6 (nand_6_out, DB, nand_3_out);
  nand nand_7 (nand_7_out, DC, DC);
  nand nand_8 (nand_8_out, d_ff_3_q, d_ff_3_q);
  nand nand_9 (nand_9_out, nand_4_out, nand_4_out);
  nand nand_10 (nand_10_out, nand_5_out, nand_6_out);
  nand nand_11 (nand_11_out, d_ff_3_q, d_ff_3_q);
  nand nand_12 (nand_12_out, nand_7_out, nand_8_out);
  nand nand_13 (nand_13_out, nand_9_out, d_ff_3_q);
  nand nand_14 (nand_14_out, nand_10_out, nand_10_out);
  nand nand_15 (nand_15_out, DB, nand_11_out);
  nand nand_16 (nand_16_out, nand_12_out, nand_13_out);
  nand nand_17 (nand_17_out, d_ff_3_q, d_ff_3_q);
  nand nand_18 (Z, nand_14_out, nand_15_out);
  nand nand_19 (nand_19_out, nand_16_out, nand_16_out);
  nand nand_20 (nand_20_out, DB, nand_17_out);
  nand nand_21 (DA, nand_19_out, nand_20_out);
  Clock clock_1 (.out(clock_1_out));
  D_Flip_Flop d_ff_1 (.clk(clock_1_out), .D(DA), .Q(DB));  // open: Qn, preset, en, reset
  D_Flip_Flop d_ff_2 (.clk(clock_1_out), .D(DB), .Q(DC));  // open: Qn, preset, en, reset
  D_Flip_Flop d_ff_3 (.clk(clock_1_out), .D(DC), .Q(d_ff_3_q));  // open: Qn, preset, en, reset
endmodule
