// Logisim project Sriman.circ as structural Verilog
module Decoder (
  input  E,
  input  X,
  input  Y,
  output D3,
  output A_B,
  output D2,
  output A_B_2,
  output D1,
  output A_B_3,
  output D0
);

  wire nand_1_out, nand_2_out, nand_3_out, nand_4_out, nand_5_out, nand_6_out, nand_7_out, nand_8_out,
       nand_13_out;

  nand nand_1 (nand_1_out, E, E);
  nand nand_2 (nand_2_out, Y, Y);
  nand nand_3 (nand_3_out, E, E);
  nand nand_4 (nand_4_out, X, X);
  nand nand_5 (nand_5_out, E, E);
  nand nand_6 (nand_6_out, Y, Y);
  nand nand_7 (nand_7_out, X, X);
  nand nand_8 (nand_8_out, E, E);
  nand nand_9 (D3, X, Y, nand_1_out);
  nand nand_10 (D2, X, nand_2_out, nand_3_out);
  nand nand_11 (D1, Y, nand_4_out, nand_5_out);
  nand nand_12 (D0, nand_6_out, nand_7_out, nand_8_out);
  not not_1 (A_B, D2);
  nand nand_13 (nand_13_out, D2, D1);
  not not_2 (A_B_3, D1);
  not not_3 (A_B_2, nand_13_out);
endmodule
